// Logisim project F6_miniRV.circ as structural Verilog: 2 circuits, main circuit miniRV
module miniRV (
  input  RUN,
  input  CLR,
  input  CLK
);

  wire or_1_out;
  wire [31:0] adder_1_out, adder_2_out, bit_extender_1_out, gpr16x32_1_rdata1, multiplexer_1_out,
       register_1_q, rom_1_data;

  or or_1 (or_1_out, RUN, CLR);
  Register #(.width(32)) register_1 (.D(multiplexer_1_out), .en(or_1_out), .clk(CLK), .Q(register_1_q));  // open: clr
  // Probe on register_1_q
  Adder #(.width(32)) adder_1 (.a(register_1_q), .b(32'h4), .out(adder_1_out));  // open: cin, cout
  Multiplexer #(.width(32)) multiplexer_1 (.in0(adder_1_out), .in1({32{1'b0}}), .out(multiplexer_1_out), .sel(CLR));
  // Probe on register_1_q[5:2]
  ROM #(.addrWidth(4), .dataWidth(32)) rom_1 (.addr(register_1_q[5:2]), .data(rom_1_data));
  // Probe on rom_1_data
  assign bit_extender_1_out = {{20{rom_1_data[31]}}, rom_1_data[31:20]};  // Bit_Extender bit_extender_1
  gpr16x32 gpr16x32_1 (
    .wdata(adder_2_out), .CLK(CLK), .waddr(rom_1_data[10:7]), .wen(1'b1), .raddr1(rom_1_data[18:15]),
    .rdata1(gpr16x32_1_rdata1));  // open: raddr2, rdata2
  // Probe on adder_2_out
  Adder #(.width(32)) adder_2 (.a(gpr16x32_1_rdata1), .b(bit_extender_1_out), .out(adder_2_out));  // open: cin, cout

  // Notes on the sheet:
  //   contents of rom_1 (hex, n*v repeats v):
  //   1400513 10000e7 c000e7 c00067 a50513 8067
endmodule

module gpr16x32 (
  input  [31:0] wdata,
  input  CLK,
  input  [3:0] waddr,
  input  wen,
  input  [3:0] raddr1,
  input  [3:0] raddr2,
  output [31:0] rdata1,
  output [31:0] rdata2
);

  wire decoder_1_out1, decoder_1_out2, decoder_1_out3, decoder_1_out4, decoder_1_out5, decoder_1_out6,
       decoder_1_out7, decoder_1_out8, decoder_1_out9, decoder_1_out10, decoder_1_out11, decoder_1_out12,
       decoder_1_out13, decoder_1_out14, decoder_1_out15;
  wire [31:0] register_1_q, register_2_q, register_3_q, register_4_q, register_5_q, register_6_q,
       register_7_q, register_8_q, register_9_q, register_10_q, register_11_q, register_12_q, register_13_q,
       register_14_q, register_15_q;

  Decoder #(.select(4)) decoder_1 (
    .out1(decoder_1_out1), .out2(decoder_1_out2), .out3(decoder_1_out3), .out4(decoder_1_out4),
    .out5(decoder_1_out5), .out6(decoder_1_out6), .out7(decoder_1_out7), .out8(decoder_1_out8),
    .out9(decoder_1_out9), .out10(decoder_1_out10), .out11(decoder_1_out11), .out12(decoder_1_out12),
    .out13(decoder_1_out13), .out14(decoder_1_out14), .out15(decoder_1_out15), .sel(waddr), .en(wen));  // open: out0
  Register #(.width(32)) register_1 (.D(wdata), .en(decoder_1_out15), .clk(CLK), .Q(register_1_q));  // open: clr
  Register #(.width(32)) register_2 (.D(wdata), .en(decoder_1_out14), .clk(CLK), .Q(register_2_q));  // open: clr
  Register #(.width(32)) register_3 (.D(wdata), .en(decoder_1_out13), .clk(CLK), .Q(register_3_q));  // open: clr
  Register #(.width(32)) register_4 (.D(wdata), .en(decoder_1_out12), .clk(CLK), .Q(register_4_q));  // open: clr
  Register #(.width(32)) register_5 (.D(wdata), .en(decoder_1_out11), .clk(CLK), .Q(register_5_q));  // open: clr
  Register #(.width(32)) register_6 (.D(wdata), .en(decoder_1_out10), .clk(CLK), .Q(register_6_q));  // open: clr
  Register #(.width(32)) register_7 (.D(wdata), .en(decoder_1_out9), .clk(CLK), .Q(register_7_q));  // open: clr
  Register #(.width(32)) register_8 (.D(wdata), .en(decoder_1_out8), .clk(CLK), .Q(register_8_q));  // open: clr
  Register #(.width(32)) register_9 (.D(wdata), .en(decoder_1_out7), .clk(CLK), .Q(register_9_q));  // open: clr
  Register #(.width(32)) register_10 (.D(wdata), .en(decoder_1_out6), .clk(CLK), .Q(register_10_q));  // open: clr
  Register #(.width(32)) register_11 (.D(wdata), .en(decoder_1_out5), .clk(CLK), .Q(register_11_q));  // open: clr
  Register #(.width(32)) register_12 (.D(wdata), .en(decoder_1_out4), .clk(CLK), .Q(register_12_q));  // open: clr
  Register #(.width(32)) register_13 (.D(wdata), .en(decoder_1_out3), .clk(CLK), .Q(register_13_q));  // open: clr
  Register #(.width(32)) register_14 (.D(wdata), .en(decoder_1_out2), .clk(CLK), .Q(register_14_q));  // open: clr
  Register #(.width(32)) register_15 (.D(wdata), .en(decoder_1_out1), .clk(CLK), .Q(register_15_q));  // open: clr
  Multiplexer #(.select(4), .width(32)) multiplexer_1 (
    .in0({32{1'b0}}), .in1(register_15_q), .in2(register_14_q), .in3(register_13_q), .in4(register_12_q),
    .in5(register_11_q), .in6(register_10_q), .in7(register_9_q), .in8(register_8_q), .in9(register_7_q),
    .in10(register_6_q), .in11(register_5_q), .in12(register_4_q), .in13(register_3_q), .in14(register_2_q),
    .in15(register_1_q), .out(rdata1), .sel(raddr1));
  Multiplexer #(.select(4), .width(32)) multiplexer_2 (
    .in0({32{1'b0}}), .in1(register_15_q), .in2(register_14_q), .in3(register_13_q), .in4(register_12_q),
    .in5(register_11_q), .in6(register_10_q), .in7(register_9_q), .in8(register_8_q), .in9(register_7_q),
    .in10(register_6_q), .in11(register_5_q), .in12(register_4_q), .in13(register_3_q), .in14(register_2_q),
    .in15(register_1_q), .out(rdata2), .sel(raddr2));
endmodule
